# Fritzing sketch Thermometer Circuit Diagram (saved by Fritzing 0.9.3b)
circuit board: 8.46667cm x 5.64444cm
breadboards: 1

parts:
  Part1 = TMP006 Thermopile Sensor
  Raspberry_Pi_1 = Raspberry Pi 3 [part_number=RPI-3-V1.2]

nets:
  VCC: Part1.VCC, Raspberry_Pi_1.3v3
  GND: Part1.GND, Raspberry_Pi_1.GND
  N1: Part1.SDA, Raspberry_Pi_1.GPIO2
  N2: Part1.SCL, Raspberry_Pi_1.GPIO3

custom parts:
  TMP006 Thermopile Sensor: Unlike all the other temperature sensors we have, this breakout has a really cool IR sensor from TI that can measure the temperature of an object without touching it! Simply point the sensor towards what you want to measure and it will detect the temperature by absorbing IR waves emitted. The embedded thermopile sensor generates a very very small voltage depending on how much IR there is, and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
